# Fritzing sketch sketch_ais (saved by Fritzing 0.9.3b)

parts:
  Mod1 = Raspberry Pi Pico
  DHT2 = Humidity and Temperature Sensor DHT11
  Part1 = MQ-9 breakout
  F1 = Fan - Ventilador [package=THT]
  Part2 = Standard LCD 16x2 white on blue [part_number=181]
  A1 = BBAA100043
  LCM1602_IIC2 = LCM1602 IIC [part_number="LCM1602 IIC" chip_label="LCM1602 IIC" package="DIP (Dual Inline) [THT]"]
  J1 = Piezo Speaker

nets:
  GND: Mod1.pin_3, Mod1.pin_13, Mod1.pin_18, Mod1.pin_33, Mod1.pin_38, DHT2.GND_1, Part1.GND, F1.GND, A1.pin4, LCM1602_IIC2.GND, J1.pin1
  N1: Mod1.pin_6, LCM1602_IIC2.SDA
  N2: Mod1.pin_7, LCM1602_IIC2.SCL
  N3: Mod1.pin_11, J1.pin2
  N4: Mod1.pin_19, F1.5V
  N5: Mod1.pin_26, A1.pin3
  N6: Mod1.pin_27, A1.pin2
  N7: Mod1.pin_29, A1.pin1
  N8: Mod1.pin_31, DHT2.Data-signal
  N9: Mod1.pin_32, Part1.AO
  VCC: Mod1.pin_37, DHT2.Vcc, Part1.VCC
  N10: Mod1.pin_40, LCM1602_IIC2.VCC
  VSS: Part2.VSS, LCM1602_IIC2.VSS
  VDD: Part2.VDD, LCM1602_IIC2.VDD
  N11: Part2.V0, LCM1602_IIC2.V0
  N12: Part2.RS, LCM1602_IIC2.RS
  N13: Part2.R/W, LCM1602_IIC2.RW
  N14: Part2.E, LCM1602_IIC2.E
  N15: Part2.DB0, LCM1602_IIC2.D0
  N16: Part2.DB1, LCM1602_IIC2.D1
  N17: Part2.DB2, LCM1602_IIC2.D2
  N18: Part2.DB3, LCM1602_IIC2.D3
  N19: Part2.DB4, LCM1602_IIC2.D4
  N20: Part2.DB5, LCM1602_IIC2.D5
  N21: Part2.DB6, LCM1602_IIC2.D6
  N22: Part2.DB7, LCM1602_IIC2.D7
  N23: Part2.LED+, LCM1602_IIC2.A
  N24: Part2.LED-, LCM1602_IIC2.K

custom parts:
  Raspberry Pi Pico: Raspberry Pi Pico. Based around the RP2040 microcontroller the Pico is a low cost microcontroller device bringing Raspberry Pi quality, cost, and easy of use to the microcontroller space. Jan 2021, Split part in to two versions: SMD (this one) and tht. This one is single sided and uses the castellation pads to solder the module to the board (no holes, other than for the USB connector!). The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
  Humidity and Temperature Sensor DHT11: Digital relative humidity & temperature sensor DHT11
  MQ-9 breakout: SKU: 101284
  Fan - Ventilador: Ventilador de 2 pines, se encuentra comunmente en computadoras de escritorio
  Standard LCD 16x2 white on blue: Standard HD44780 LCDs are useful for creating standalone projects. * 16 characters wide, 2 rows * White text on blue background * Connection port is 0.1" pitch, single row for easy breadboarding and wiring
  BBAA100043: BBAA100043 traffic light module.
  LCM1602 IIC: I2C-Module to use a 1602 or 2004 LCD on with the wire.h libory Serial LCD Modul
